# Fritzing sketch sketch (saved by Fritzing 0.9.3b)
breadboards: 1

parts:
  U1 = ESP8266 NodeMCU LoLin module
  OLED_I2C1 = OLED 128x64 I2C Monochrome Display
  buz1 = Piezo Buzzer

nets:
  N1: U1.D1, OLED_I2C1.SCK
  N2: U1.D2, OLED_I2C1.SDA
  N3: U1.D3, buz1.pin_2
  3V3: U1.3V3, OLED_I2C1.VDD
  GND: U1.GND, OLED_I2C1.GND, buz1.pin_1

custom parts:
  ESP8266 NodeMCU LoLin module: ESP8266 based NodeMCU
  Piezo Buzzer: Part from https://www.nutsvolts.com/magazine/article/november2012_SmileysWorkshop. Breadboard and icon images modified to be 0.3" in spacing and be more similar to the actual physical part.
